# Fritzing sketch rangkaian (saved by Fritzing 0.9.3b)

parts:
  U1 = ESP32-38PinWide [part_number=ESP32-38PinWide]
  J1 = STM32 Nucleo boards
  M1 = fc-51 [package=THT]
  C1 = Electrolytic Capacitor [package="2cm H-Type"]
  DHT1 = DHT22 Humidity and Temperature Sensor
  M3 = ac light dimmer-4terminal
  Mod1 = KY-018 Photoresistor Module [package="Breakout board"]
  Part1 = KY-037 High Sensitivity Sound Detection Module [package="Breakout board"]
  Power_plug1 = Power plug
  SPKR1 = Loudspeaker
  DFRobot_DFPlayer_Mini1 = DFRobot DFPlayer Mini [part_number=DFR0299]
  U3 = LM2596 step down module
  Part2 = Mono 2.5W Class D Audio Amplifier - PAM8302
  D2 = LTE-302 [package=lte-302]
  KF-1 = KF-301 Relay [package=THT]
  M4 = DC Motor

nets:
  GND: U1.GPIO11, J1.GND, M1.pin2, DHT1.GND, M3.GND, Mod1.-, Part1.G, Power_plug1.GND, DFRobot_DFPlayer_Mini1.GND-1, DFRobot_DFPlayer_Mini1.GND-2, U3.IN-, U3.OUT-, Part2.GND, Part2.AIN-, KF-1.ground
  VIN: U1.VIN, J1.VIN, Power_plug1.VCC, U3.IN+
  N1: U1.GPIO16, J1.PA9
  N2: U1.GPIO17, J1.PA10
  N3: J1.A1, Mod1.S
  N4: J1.A2, Part1.A0
  N5: J1.PB11, DFRobot_DFPlayer_Mini1.TX
  N6: J1.D9_PWM, M1.pin1
  N7: J1.D2, M3.Z-C
  N8: J1.D4, DHT1.DATA
  N9: J1.D6_PWM, KF-1.signal
  N10: J1.PB10, DFRobot_DFPlayer_Mini1.RX
  VCC: M1.pin3, DHT1.VDD, M3.VCC, Mod1.Vin, Part1.+, DFRobot_DFPlayer_Mini1.VCC, U3.OUT+, Part2.VCC, KF-1.power
  N11: C1.-, Part2.AIN+
  N12: C1.+, DFRobot_DFPlayer_Mini1.DAC_L
  N13: M3.LOAD1, D2.A
  N14: M3.LOAD2, D2.C
  N15: SPKR1.pin1, Part2.VO-
  N16: SPKR1.pin2, Part2.VO+
  N17: KF-1.NO, M4.pin_2

notes:
  220vac

custom parts:
  ESP32-38PinWide: Generic 38-Pin ESP32 with wide format (only access to one side of pins on a breadboard) based on Stephen Lilley's HiLetgo ESP-WROOM-32 ESP32 ESP-32S Development Board.
  ac light dimmer-4terminal: ac light dimmer module 4terminal.
  KY-018 Photoresistor Module: KY-018 Photoresistor module, used to measure light intensity. It can determine the presence or absence of light.
  KY-037 High Sensitivity Sound Detection Module: KY-037 high sensitivity sound detection module is an analog/digital sensor that uses a condenser microphone to observe changes in environment noise.
  LM2596 step down module: LM2596 DC-DC step down power supply module 3 A.
  Mono 2.5W Class D Audio Amplifier - PAM8302: A super small but powerful mono amplifier able to deliver up to 2.5 Watts into 4-8 ohm impedance speakers. Inside the miniature chip is a class D controller, able to run from 2.0V-5.5VDC. Since the amp is a class D, its very efficient (over 90% efficient when driving an 8Ω speaker at over half a Watt) - making it perfect for portable and battery-powered projects.
  KF-301 Relay: KF-301
